// Logisim project bfcpu.circ as structural Verilog: 6 circuits, main circuit Register4
module main (
  input  RESET,
  input  EN_D,
  input  EN_DP,
  input  EN_SP,
  input  EN_F,
  input  EN_I,
  input  EN_IP,
  input  EN_LS,
  input  LD_D,
  input  LD_DP,
  input  LD_SP,
  input  LD_F,
  input  LD_I,
  input  LD_IP,
  input  LD_LS,
  input  [2:0] RS,
  input  INC,
  input  DEC,
  input  WE,
  input  OE,
  input  PRE,
  input  [3:0] in_22,
  input  [3:0] in_23
);

  wire CLC, RESET_t;
  wire [1:0] DPREG, DREG, FREG, IPREG, IREG, LSREG, SPREG;
  wire [7:0] D_d_out, IP_d_out, RAM1_dout, RAM2_dout;
  wire [15:0] DP_d_out;

  Clock clock_1 (.out(CLC));
  Register4 F ();  // open: EN, LD, DN, UP, D_IN, RESET, Z, D_OUT
  ControlUnit controlunit_1 (
    .CLC(CLC), .CMD(in_22), .FLAGS(in_23));  // open: RS, INC, DEC, EN_D, EN_DP, EN_IP, EN_SP, OE_RAM, WE_RAM, LD_D, LD_IP, LD_I, LD_F, CR, VE, AE, PRE, ERR
  Register8 I ();  // open: RESET, EN, LD, DN, UP, D_IN, Z, D_OUT
  TTY tty_1 (.clk(CLC), .we(PRE), .clr(RESET_t));  // open: data
  RegisterDriver registerdriver_1 (
    .INC(INC), .DEC(DEC), .CLC(CLC), .RS(RS), .R0(DREG), .R1(DPREG), .R2(SPREG), .R3(FREG), .R4(IREG),
    .R5(IPREG), .R6(LSREG));  // open: R7
  Register8 LS ();  // open: RESET, EN, LD, DN, UP, D_IN, Z, D_OUT
  RAM #(.addrWidth(16), .clearpin("true")) RAM1 (
    .addr(DP_d_out), .we(WE), .oe(OE), .clk(CLC), .din(D_d_out), .dout(RAM1_dout), .clr(RESET));
  Register16 DP (
    .D_IN(16'h100), .EN(EN_DP), .LD(RESET), .DN(DPREG[0]), .UP(DPREG[1]), .D_OUT(DP_d_out));  // open: RESET, Z
  Register8 D (
    .RESET(RESET), .EN(EN_D), .LD(LD_D), .DN(DREG[0]), .UP(DREG[1]), .D_IN(RAM1_dout), .D_OUT(D_d_out));  // open: Z
  RAM #(.addrWidth(16), .clearpin("true")) RAM2 (
    .addr(DP_d_out), .we(WE), .oe(OE), .clk(CLC), .din(IP_d_out), .dout(RAM2_dout), .clr(RESET));
  Register16 SP (
    .RESET(RESET), .EN(EN_SP), .LD(LD_SP), .DN(SPREG[0]), .UP(SPREG[1]), .D_OUT(DP_d_out));  // open: D_IN, Z
  Register16 IP (
    .D_IN({RAM1_dout, RAM2_dout}), .RESET(RESET), .EN(EN_IP), .LD(LD_IP), .DN(IPREG[0]), .UP(IPREG[1]),
    .D_OUT({IP_d_out, D_d_out}));  // open: Z

  // Other names for the same wires on the sheet: R = RESET

  // Notes on the sheet:
  //   RESET VECTOR
endmodule

module Register4 (
  input  EN,
  input  LD,
  input  DN,
  input  UP,
  input  [3:0] D_IN,
  input  RESET,
  output [3:0] D_OUT,
  output Z
);

  wire n74193_1_pin11;
  wire [3:0] n74193_1_pin3;

  _74193 u_74193_1 (
    .pin1(D_IN[1]), .pin2(n74193_1_pin3[1]), .pin3(n74193_1_pin3[0]), .pin4(DN), .pin5(UP),
    .pin6(n74193_1_pin3[2]), .pin7(n74193_1_pin3[3]), .pin15(D_IN[0]), .pin14(RESET), .pin11(n74193_1_pin11),
    .pin10(D_IN[2]), .pin9(D_IN[3]));  // open: pin13, pin12
  not not_1 (n74193_1_pin11, LD);
  Hex_Digit_Display hex_digit_display_1 (.value(n74193_1_pin3));  // open: dp
  nor nor_1 (Z, n74193_1_pin3[3], n74193_1_pin3[2], n74193_1_pin3[1], n74193_1_pin3[0]);
  assign D_OUT = EN ? n74193_1_pin3 : 4'bz;  // Controlled_Buffer controlled_buffer_1
endmodule

module Register8 (
  input  [7:0] D_IN,
  input  EN,
  input  LD,
  input  DN,
  input  UP,
  input  RESET,
  output [7:0] D_OUT,
  output Z
);

  wire n74193_1_pin11, n74193_1_pin12, n74193_1_pin13, n74193_2_pin11, or_1_out, or_2_out;
  wire [3:0] n74193_1_pin3, n74193_2_pin3;

  _74193 u_74193_1 (
    .pin1(D_IN[1]), .pin2(n74193_1_pin3[1]), .pin3(n74193_1_pin3[0]), .pin4(DN), .pin5(UP),
    .pin6(n74193_1_pin3[2]), .pin7(n74193_1_pin3[3]), .pin15(D_IN[0]), .pin14(RESET), .pin13(n74193_1_pin13),
    .pin12(n74193_1_pin12), .pin11(n74193_1_pin11), .pin10(D_IN[2]), .pin9(D_IN[3]));
  not not_1 (n74193_1_pin11, LD);
  Hex_Digit_Display hex_digit_display_1 (.value(n74193_1_pin3));  // open: dp
  or or_1 (or_1_out, n74193_1_pin3[3], n74193_1_pin3[2], n74193_1_pin3[1], n74193_1_pin3[0]);
  assign D_OUT[7:4] = EN ? n74193_1_pin3 : 4'bz;  // Controlled_Buffer controlled_buffer_1
  _74193 u_74193_2 (
    .pin1(D_IN[5]), .pin2(n74193_2_pin3[1]), .pin3(n74193_2_pin3[0]), .pin4(n74193_1_pin13),
    .pin5(n74193_1_pin12), .pin6(n74193_2_pin3[2]), .pin7(n74193_2_pin3[3]), .pin15(D_IN[4]), .pin14(RESET),
    .pin11(n74193_2_pin11), .pin10(D_IN[6]), .pin9(D_IN[7]));  // open: pin13, pin12
  not not_2 (n74193_2_pin11, LD);
  Hex_Digit_Display hex_digit_display_2 (.value(n74193_2_pin3));  // open: dp
  or or_2 (or_2_out, n74193_2_pin3[3], n74193_2_pin3[2], n74193_2_pin3[1], n74193_2_pin3[0]);
  assign D_OUT[3:0] = EN ? n74193_2_pin3 : 4'bz;  // Controlled_Buffer controlled_buffer_2
  nor nor_1 (Z, or_2_out, or_1_out);

  // Other names for the same wires on the sheet: R = RESET
endmodule

module Register16 (
  input  [15:0] D_IN,
  input  EN,
  input  LD,
  input  DN,
  input  UP,
  input  RESET,
  output [15:0] D_OUT,
  output Z
);

  wire n74193_1_pin11, n74193_1_pin12, n74193_1_pin13, n74193_2_pin11, n74193_2_pin12, n74193_2_pin13,
       n74193_3_pin11, n74193_3_pin12, n74193_3_pin13, n74193_4_pin11, or_1_out, or_2_out, or_3_out, or_4_out;
  wire [3:0] n74193_1_pin3, n74193_2_pin3, n74193_3_pin3, n74193_4_pin3;

  _74193 u_74193_1 (
    .pin1(D_IN[1]), .pin2(n74193_1_pin3[1]), .pin3(n74193_1_pin3[0]), .pin4(DN), .pin5(UP),
    .pin6(n74193_1_pin3[2]), .pin7(n74193_1_pin3[3]), .pin15(D_IN[0]), .pin14(RESET), .pin13(n74193_1_pin13),
    .pin12(n74193_1_pin12), .pin11(n74193_1_pin11), .pin10(D_IN[2]), .pin9(D_IN[3]));
  not not_1 (n74193_1_pin11, LD);
  or or_1 (or_1_out, n74193_1_pin3[3], n74193_1_pin3[2], n74193_1_pin3[1], n74193_1_pin3[0]);
  Hex_Digit_Display hex_digit_display_1 (.value(n74193_1_pin3));  // open: dp
  assign D_OUT[3:0] = EN ? n74193_1_pin3 : 4'bz;  // Controlled_Buffer controlled_buffer_1
  _74193 u_74193_2 (
    .pin1(D_IN[5]), .pin2(n74193_2_pin3[1]), .pin3(n74193_2_pin3[0]), .pin4(n74193_1_pin13),
    .pin5(n74193_1_pin12), .pin6(n74193_2_pin3[2]), .pin7(n74193_2_pin3[3]), .pin15(D_IN[4]), .pin14(RESET),
    .pin13(n74193_2_pin13), .pin12(n74193_2_pin12), .pin11(n74193_2_pin11), .pin10(D_IN[6]), .pin9(D_IN[7]));
  not not_2 (n74193_2_pin11, LD);
  Hex_Digit_Display hex_digit_display_2 (.value(n74193_2_pin3));  // open: dp
  or or_2 (or_2_out, n74193_2_pin3[3], n74193_2_pin3[2], n74193_2_pin3[1], n74193_2_pin3[0]);
  assign D_OUT[7:4] = EN ? n74193_2_pin3 : 4'bz;  // Controlled_Buffer controlled_buffer_2
  _74193 u_74193_3 (
    .pin1(D_IN[9]), .pin2(n74193_3_pin3[1]), .pin3(n74193_3_pin3[0]), .pin4(n74193_2_pin13),
    .pin5(n74193_2_pin12), .pin6(n74193_3_pin3[2]), .pin7(n74193_3_pin3[3]), .pin15(D_IN[8]), .pin14(RESET),
    .pin13(n74193_3_pin13), .pin12(n74193_3_pin12), .pin11(n74193_3_pin11), .pin10(D_IN[10]), .pin9(D_IN[11]));
  not not_3 (n74193_3_pin11, LD);
  Hex_Digit_Display hex_digit_display_3 (.value(n74193_3_pin3));  // open: dp
  or or_3 (or_3_out, n74193_3_pin3[3], n74193_3_pin3[2], n74193_3_pin3[1], n74193_3_pin3[0]);
  assign D_OUT[11:8] = EN ? n74193_3_pin3 : 4'bz;  // Controlled_Buffer controlled_buffer_3
  _74193 u_74193_4 (
    .pin1(D_IN[13]), .pin2(n74193_4_pin3[1]), .pin3(n74193_4_pin3[0]), .pin4(n74193_3_pin13),
    .pin5(n74193_3_pin12), .pin6(n74193_4_pin3[2]), .pin7(n74193_4_pin3[3]), .pin15(D_IN[12]), .pin14(RESET),
    .pin11(n74193_4_pin11), .pin10(D_IN[14]), .pin9(D_IN[15]));  // open: pin13, pin12
  not not_4 (n74193_4_pin11, LD);
  Hex_Digit_Display hex_digit_display_4 (.value(n74193_4_pin3));  // open: dp
  or or_4 (or_4_out, n74193_4_pin3[3], n74193_4_pin3[2], n74193_4_pin3[1], n74193_4_pin3[0]);
  assign D_OUT[15:12] = EN ? n74193_4_pin3 : 4'bz;  // Controlled_Buffer controlled_buffer_4
  nor nor_1 (Z, or_4_out, or_3_out, or_2_out, or_1_out);

  // Other names for the same wires on the sheet: R = RESET
endmodule

module RegisterDriver (
  input  INC,
  input  DEC,
  input  CLC,
  input  [2:0] RS,
  output [1:0] R0,
  output [1:0] R1,
  output [1:0] R2,
  output [1:0] R3,
  output [1:0] R4,
  output [1:0] R5,
  output [1:0] R6,
  output [1:0] R7
);

  wire and_1_out, not_1_out, not_2_out, xor_1_out;
  wire [1:0] nand_1_out;

  xor xor_1 (xor_1_out, DEC, INC);
  not not_1 (not_1_out, INC);
  not not_2 (not_2_out, DEC);
  and and_1 (and_1_out, xor_1_out, CLC);
  nand nand_1 (nand_1_out[0], not_1_out, and_1_out);
  nand nand_2 (nand_1_out[1], not_2_out, and_1_out);
  Demultiplexer #(.select(3), .width(2)) demultiplexer_1 (
    .out0(R0), .out1(R1), .out2(R2), .out3(R3), .out4(R4), .out5(R5), .out6(R6), .out7(R7), .in(nand_1_out),
    .sel(RS));
endmodule

module ControlUnit (
  input  [3:0] CMD,
  input  [3:0] FLAGS,
  input  CLC,
  output [2:0] RS,
  output INC,
  output DEC,
  output EN_D,
  output EN_DP,
  output EN_IP,
  output EN_SP,
  output OE_RAM,
  output WE_RAM,
  output LD_D,
  output LD_IP,
  output LD_I,
  output LD_F,
  output CR,
  output VE,
  output AE,
  output PRE,
  output ERR
);

  wire n74163_1_pin1, n74163_1_pin7, not_2_out;
  wire [2:0] n74163_1_pin14;
  wire [3:3] n74163_1_pin11;
  wire [7:4] ROM3_data;

  ROM #(.addrWidth(13)) ROM1 (.addr({2'b00, CMD, n74163_1_pin14, FLAGS}), .data({EN_IP, EN_DP, EN_D, DEC, INC, RS}));
  ROM #(.addrWidth(13)) ROM2 (
    .addr({2'b00, CMD, n74163_1_pin14, FLAGS}), .data({CR, LD_F, LD_I, LD_IP, LD_D, WE_RAM, OE_RAM, EN_SP}));
  _74163 u_74163_1 (
    .pin1(n74163_1_pin1), .pin2(CLC), .pin7(n74163_1_pin7), .pin14(n74163_1_pin14[0]),
    .pin13(n74163_1_pin14[1]), .pin12(n74163_1_pin14[2]), .pin11(n74163_1_pin11[3]), .pin10(n74163_1_pin7));  // open: pin3, pin4, pin5, pin6, pin15, pin9
  not not_1 (n74163_1_pin1, CR);
  not not_2 (not_2_out, ERR);
  LED led_1 (.in(not_2_out));
  LED led_2 (.in(ERR));
  Hex_Digit_Display hex_digit_display_1 (.value({n74163_1_pin11[3], n74163_1_pin14}));  // open: dp
  ROM #(.addrWidth(13)) ROM3 (.addr({2'b00, CMD, n74163_1_pin14, FLAGS}), .data({ROM3_data, ERR, PRE, AE, VE}));
  // also tied to VCC on the sheet: n74163_1_pin7

  // Notes on the sheet:
  //   contents of ROM1 (hex, n*v repeats v):
  //   16*80 112*0 16*80 d d 8 8 d d 40 40 d d 8 8 d d 40 40 0 0 d d 6*0 d d 84*0 16*80 d d 10 10 d d 40 40
  //   d d 10 10 d d 40 40 0 0 d d 6*0 d d 84*0 16*80 d d 11 11 d d 11 11 d d 60 60 d d 60 60 0 0 d d 0 0 d
  //   d 88*0 16*80 d d 9 9 d d 9 9 d d 60 60 d d 60 60 0 0 d d 0 0 d d 88*0 16*80 112*0 16*80 d d 2d 2d d
  //   d 40 40 d d 2d 2d d d 40 40 6*0 2d 2d 6*0 2d 2d 80*0 16*80 e e a e e e 40 40 e e a e e e 40 40 d d
  //   80 b d d 0 0 d d 80 b d d 4*0 d 7*0 d 69*0 16*80 16 16 0 12 16 16 40 40 16 16 0 12 16 16 40 40 6*d 0
  //   0 6*d 82*0 16*80 112*0 16*80 112*0 16*80 112*0 16*80 112*0 16*80 112*0 16*80 112*0 16*80
  //   Cycle Count
  //   contents of ROM2 (hex, n*v repeats v):
  //   16*20 112*80 16*20 80 80 40 40 80 80 ca ca 80 80 40 40 80 80 ca ca 96*80 16*20 80 80 40 40 80 80 ca
  //   ca 80 80 40 40 80 80 ca ca 96*80 16*20 80 80 40 40 80 80 40 40 80 80 c4 c4 80 80 c4 c4 96*80 16*20
  //   80 80 40 40 80 80 40 40 80 80 c4 c4 80 80 c4 c4 96*80 16*20 112*80 16*20 6*80 a a 6*80 a a 96*80
  //   16*20 6*0 a a 6*0 a a 80 80 5 80 80 80 c0 c0 80 80 5 80 80 80 c0 c0 80*80 16*20 0 0 13 0 0 0 a a 0 0
  //   13 0 0 0 a a 6*80 c0 c0 6*80 c0 c0 80*80 16*20 112*80 16*20 112*80 16*20 112*80 16*20 112*80 16*20
  //   112*80 16*20 112*80 16*20 112*80
  //   contents of ROM3 (hex, n*v repeats v):
  //   16*0 112*8 18*0 1 1 6*0 1 1 4*0 8 8 0 0 6*8 0 0 84*8 18*0 1 1 6*0 1 1 4*0 8 8 0 0 6*8 0 0 84*8 18*0
  //   2 2 0 0 2 2 8*0 8 8 0 0 8 8 0 0 88*8 18*0 2 2 0 0 2 2 8*0 8 8 0 0 8 8 0 0 88*8 16*0 112*8 18*0 4 4
  //   6*0 4 4 4*0 6*8 4 4 6*8 4 4 80*8 48*0 8 8 0 7*8 0 69*8 48*0 80*8 16*0 112*8 16*0 112*8 16*0 112*8
  //   16*0 112*8 16*0 112*8 16*0 112*8 16*0 112*8
endmodule
